# Fritzing sketch ArduinoMega (saved by Fritzing 0.9.3b)
breadboards: 1

parts:
  Parça3 = Arduino Mega 2560 (Rev3)
  LCD2 = LCD screen
  LCM1602_IIC1 = LCM1602 IIC [part_number="LCM1602 IIC" chip_label="LCM1602 IIC" package="DIP (Dual Inline) [THT]"]
  SD_card_module1 = SD Card Module  # not connected
  S1 = H-Bridge with L298N
  J1 = Basic Servo
  hc-sr1 = hc-sr04
  M1 = DC Motor

nets:
  N1: Parça3.A2, S1.ENB
  N2: Parça3.D21/SCL, LCM1602_IIC1.SCL
  N3: Parça3.D20/SDA, LCM1602_IIC1.SDA
  5V: Parça3.5V, LCM1602_IIC1.VCC, S1.5V, hc-sr1.VCC
  GND: Parça3.GND, LCM1602_IIC1.GND, S1.GND, hc-sr1.GND
  N4: Parça3.D2_PWM, hc-sr1.Trig
  N5: Parça3.D3_PWM, hc-sr1.Echo
  N6: Parça3.D5_PWM, S1.IN3
  N7: Parça3.D6_PWM, S1.IN4
  N8: Parça3.D7_PWM, J1.pulse
  VSS: LCD2.VSS, LCM1602_IIC1.VSS
  VDD: LCD2.VDD, LCM1602_IIC1.VDD
  N9: LCD2.V0, LCM1602_IIC1.V0
  N10: LCD2.RS, LCM1602_IIC1.RS
  N11: LCD2.R/W, LCM1602_IIC1.RW
  N12: LCD2.E, LCM1602_IIC1.E
  N13: LCD2.DB0, LCM1602_IIC1.D0
  N14: LCD2.DB1, LCM1602_IIC1.D1
  N15: LCD2.DB2, LCM1602_IIC1.D2
  N16: LCD2.DB3, LCM1602_IIC1.D3
  N17: LCD2.DB4, LCM1602_IIC1.D4
  N18: LCD2.DB5, LCM1602_IIC1.D5
  N19: LCD2.DB6, LCM1602_IIC1.D6
  N20: LCD2.DB7, LCM1602_IIC1.D7
  N21: LCD2.LED+, LCM1602_IIC1.A
  N22: LCD2.LED-, LCM1602_IIC1.K
  N23: LCM1602_IIC1.LED_A, LCM1602_IIC1.LED_B
  N24: S1.M1-01, M1.pin_2
  N25: S1.M1-02, M1.pin_1

custom parts:
  LCM1602 IIC: I2C-Module to use a 1602 or 2004 LCD on with the wire.h libory Serial LCD Modul
  SD Card Module: SD Card Module Slot Socket Reader For Arduino ARM MCU
  H-Bridge with L298N: h-bridge
